# Fritzing sketch Somfy Remote Fritzing Sketch (saved by Fritzing 0.9.6b)
circuit board: 4.19303cm x 3.93498cm
breadboards: 1

parts:
  fs1000a = FS1000A - 433Mhz RF Transmitter [package=THT]
  WeMos_D1_Mini1 = WeMos D1 Mini

nets:
  N1: fs1000a.DATA, WeMos_D1_Mini1.D4
  VCC: fs1000a.VCC, WeMos_D1_Mini1.5V
  N2: fs1000a.GND, WeMos_D1_Mini1.G

notes:
  433.42 MHz

custom parts:
  FS1000A - 433Mhz RF Transmitter: This is 433Mhz RF transmitter with receiver kit for Arduino ARM MCU wireless Application environment: Remote control switch, receiver module, motorcycles, automobile anti-theft products, home security products, electric doors, shutter doors, windows, remote control socket, remote control LED, remote audio remote control electric doors, garage door remote control, remote control retractable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
